# Fritzing sketch sketch (saved by Fritzing 0.9.3b)
breadboards: 1

parts:
  Часть1 = Arduino Nano (Rev3.0)
  Raspberry_Pi_1 = Raspberry Pi 3 [part_number=RPI-3-V1.2]  # not connected
  HC-SR50_(PCB_mounted) = mystery part, 3 pins
  DHT22_(PCB_mounted) = mystery part, 3 pins
  USBTTL1 = USB A Plug
  USBTTL2 = Micro USB B Plug

nets:
  N1: Часть1.GND, HC-SR50_(PCB_mounted).pin3, DHT22_(PCB_mounted).pin3
  N2: Часть1.D2, DHT22_(PCB_mounted).pin1
  N3: Часть1.5V, HC-SR50_(PCB_mounted).pin1, DHT22_(PCB_mounted).pin2
  N4: Часть1.A0, HC-SR50_(PCB_mounted).pin2
  N5: USBTTL1.usb, USBTTL2.usb
